// Logisim project ULA.circ as structural Verilog: 3 circuits, main circuit main
module main (
  input  [7:0] A,
  input  [7:0] B,
  input  [2:0] M_S1_S0,
  output [7:0] \saída ,
  output c_out
);

  wire and_1_out;
  wire [7:0] extensor_aritimetico_8_yi, \extensor_lógico_8_out_6 ;

  \Extensor_lógico  \extensor_lógico_1  (
    .S0(M_S1_S0[0]), .S1(M_S1_S0[1]), .M(M_S1_S0[2]), .ai(A[7]), .bi(B[7]),
    .out_6(\extensor_lógico_8_out_6 [7]));
  Extensor_Aritimetico extensor_aritimetico_1 (
    .S0(M_S1_S0[0]), .S1(M_S1_S0[1]), .M(M_S1_S0[2]), .bi(B[7]), .yi(extensor_aritimetico_8_yi[7]));
  \Extensor_lógico  \extensor_lógico_2  (
    .S0(M_S1_S0[0]), .S1(M_S1_S0[1]), .M(M_S1_S0[2]), .ai(A[6]), .bi(B[6]),
    .out_6(\extensor_lógico_8_out_6 [6]));
  Extensor_Aritimetico extensor_aritimetico_2 (
    .S0(M_S1_S0[0]), .S1(M_S1_S0[1]), .M(M_S1_S0[2]), .bi(B[6]), .yi(extensor_aritimetico_8_yi[6]));
  \Extensor_lógico  \extensor_lógico_3  (
    .S0(M_S1_S0[0]), .S1(M_S1_S0[1]), .M(M_S1_S0[2]), .ai(A[5]), .bi(B[5]),
    .out_6(\extensor_lógico_8_out_6 [5]));
  Extensor_Aritimetico extensor_aritimetico_3 (
    .S0(M_S1_S0[0]), .S1(M_S1_S0[1]), .M(M_S1_S0[2]), .bi(B[5]), .yi(extensor_aritimetico_8_yi[5]));
  Extensor_Aritimetico extensor_aritimetico_4 (
    .S0(M_S1_S0[0]), .S1(M_S1_S0[1]), .M(M_S1_S0[2]), .bi(B[4]), .yi(extensor_aritimetico_8_yi[4]));
  \Extensor_lógico  \extensor_lógico_4  (
    .S0(M_S1_S0[0]), .S1(M_S1_S0[1]), .M(M_S1_S0[2]), .ai(A[4]), .bi(B[4]),
    .out_6(\extensor_lógico_8_out_6 [4]));
  \Extensor_lógico  \extensor_lógico_5  (
    .S0(M_S1_S0[0]), .S1(M_S1_S0[1]), .M(M_S1_S0[2]), .ai(A[3]), .bi(B[3]),
    .out_6(\extensor_lógico_8_out_6 [3]));
  Extensor_Aritimetico extensor_aritimetico_5 (
    .S0(M_S1_S0[0]), .S1(M_S1_S0[1]), .M(M_S1_S0[2]), .bi(B[3]), .yi(extensor_aritimetico_8_yi[3]));
  \Extensor_lógico  \extensor_lógico_6  (
    .S0(M_S1_S0[0]), .S1(M_S1_S0[1]), .M(M_S1_S0[2]), .ai(A[2]), .bi(B[2]),
    .out_6(\extensor_lógico_8_out_6 [2]));
  Extensor_Aritimetico extensor_aritimetico_6 (
    .S0(M_S1_S0[0]), .S1(M_S1_S0[1]), .M(M_S1_S0[2]), .bi(B[2]), .yi(extensor_aritimetico_8_yi[2]));
  Extensor_Aritimetico extensor_aritimetico_7 (
    .S0(M_S1_S0[0]), .S1(M_S1_S0[1]), .M(M_S1_S0[2]), .bi(B[1]), .yi(extensor_aritimetico_8_yi[1]));
  \Extensor_lógico  \extensor_lógico_7  (
    .S0(M_S1_S0[0]), .S1(M_S1_S0[1]), .M(M_S1_S0[2]), .ai(A[1]), .bi(B[1]),
    .out_6(\extensor_lógico_8_out_6 [1]));
  Extensor_Aritimetico extensor_aritimetico_8 (
    .S0(M_S1_S0[0]), .S1(M_S1_S0[1]), .M(M_S1_S0[2]), .bi(B[0]), .yi(extensor_aritimetico_8_yi[0]));
  \Extensor_lógico  \extensor_lógico_8  (
    .S0(M_S1_S0[0]), .S1(M_S1_S0[1]), .M(M_S1_S0[2]), .ai(A[0]), .bi(B[0]),
    .out_6(\extensor_lógico_8_out_6 [0]));
  Adder adder_1 (
    .a(extensor_aritimetico_8_yi), .b(\extensor_lógico_8_out_6 ), .out(\saída ), .cin(and_1_out), .cout(c_out));
  and and_1 (and_1_out, M_S1_S0[1], M_S1_S0[2]);
endmodule

module Extensor_Aritimetico (
  input  bi,
  input  S0,
  input  S1,
  input  M,
  output yi
);

  wire and_1_out, and_2_out, not_1_out, not_2_out, not_3_out;

  not not_1 (not_1_out, S0);
  not not_2 (not_2_out, S1);
  not not_3 (not_3_out, bi);
  and and_1 (and_1_out, M, not_1_out, not_3_out);
  and and_2 (and_2_out, M, not_2_out, bi);
  or or_1 (yi, and_2_out, and_1_out);
endmodule

module \Extensor_lógico  (
  input  ai,
  input  bi,
  input  S0,
  input  S1,
  input  M,
  output out_6
);

  wire and_1_out, and_2_out, and_3_out, and_4_out, and_5_out, not_1_out, not_2_out, not_3_out, not_4_out,
       or_1_out, or_3_out;

  not not_1 (not_1_out, ai);
  not not_2 (not_2_out, S0);
  not not_3 (not_3_out, S1);
  not not_4 (not_4_out, M);
  and and_1 (and_1_out, not_4_out, not_3_out, not_2_out, not_1_out);
  and and_2 (and_2_out, not_4_out, S1, S0, bi);
  or or_1 (or_1_out, and_1_out, and_2_out, and_3_out);
  and and_3 (and_3_out, not_4_out, S0, ai, bi);
  or or_2 (out_6, or_1_out, or_3_out);
  and and_4 (and_4_out, not_4_out, S1, ai);
  or or_3 (or_3_out, and_4_out, and_5_out);
  and and_5 (and_5_out, M, ai);
endmodule
